# Fritzing sketch Licht folgi bauplan (saved by Fritzing 0.9.2b)
breadboards: 1

parts:
  Bauteil2 = Arduino Uno (Rev3)
  R1 = Photocell (LDR) [package=THT]
  R2 = Photocell (LDR) [package=THT]
  R3 = Resistor [tolerance=±5% resistance=10k package=THT]
  R5 = Resistor [tolerance=±5% resistance=10k package=THT]
  J1 = Basic Servo

nets:
  N1: Bauteil2.A0, R1.pin_0, R3.Pin_1
  N2: Bauteil2.A1, R2.pin_0, R5.Pin_1
  N3: Bauteil2.D9_PWM, J1.pulse
  GND: Bauteil2.GND, R3.Pin_0, R5.Pin_0, J1.gnd
  5V: Bauteil2.5V, R1.pin_1, R2.pin_1, J1.vcc
